// Logisim project processor.circ as structural Verilog: 6 circuits, main circuit main
module main (
  input  reset
);

  wire alu_1_zero, ALUsrc, and_1_out, Branch, clk, Display, Input, J, Jal, Jr, keyboard_1_avail, MemRd,
       MemWt, MtR, not_2_out, not_3_out, RegDst, RegWrt;
  wire [2:0] multiplexer_1_out, multiplexer_3_out, rd, rs, rt, Shamt;
  wire [3:0] ALUop, instruction_decoder_1_opcode;
  wire [5:0] Imm;
  wire [6:0] keyboard_1_data;
  wire [7:7] not_1_out;
  wire [11:0] Add;
  wire [15:0] adder_1_out, adder_2_out, alu_1_result, bit_extender_2_out, bit_extender_3_out,
       bit_extender_4_out, InputVal, multiplexer_2_out, multiplexer_4_out, multiplexer_5_out,
       multiplexer_6_out, multiplexer_7_out, multiplexer_8_out, multiplexer_9_out, PC_q, ram_1_data,
       registerfile_1_rtval, rom_1_data, rsVal;

  Clock clock_1 (.out(clk));
  Keyboard keyboard_1 (.clk(clk), .re(Input), .clr(reset), .avail(keyboard_1_avail), .data(keyboard_1_data));
  Register #(.width(16)) PC (.D(multiplexer_7_out), .en(1'b1), .Q(PC_q), .clk(clk), .clr(reset));
  not not_1 (not_1_out[7], keyboard_1_avail);
  Adder #(.width(16)) adder_1 (.a(16'h1), .b(PC_q), .out(adder_1_out));  // open: cin, cout
  ROM #(.addrWidth(16), .dataWidth(16)) rom_1 (.addr(PC_q), .data(rom_1_data));  // open: sel
  assign InputVal = {{8{not_1_out[7]}}, {not_1_out[7], keyboard_1_data}};  // Bit_Extender bit_extender_1
  Instruction_Decoder instruction_decoder_1 (
    .Instruction(rom_1_data), .Opcode(instruction_decoder_1_opcode), .shamt(Shamt), .rd(rd), .rt(rt),
    .rs(rs), .Imm(Imm), .Address(Add));
  Controller controller_1 (
    .Opcode(instruction_decoder_1_opcode), .RegWrt(RegWrt), .Branch(Branch), .MemRead(MemRd), .MemtoReg(MtR),
    .ALUop(ALUop), .MemWrite(MemWt), .ALUsrc(ALUsrc), .RegDst(RegDst), .Jump(J), .JR(Jr), .Jal(Jal),
    .Display(Display), .Input(Input));
  TTY #(.rows(13), .cols(80), .trigger("falling")) tty_1 (.data(rsVal[6:0]), .clk(clk), .we(Display), .clr(reset));
  Multiplexer #(.width(3), .enable("false")) multiplexer_1 (.in0(rt), .in1(rd), .out(multiplexer_1_out), .sel(RegDst));
  Multiplexer #(.width(16), .enable("false")) multiplexer_2 (
    .in0(multiplexer_9_out), .in1(adder_1_out), .out(multiplexer_2_out), .sel(Jal));
  Multiplexer #(.width(3), .enable("false")) multiplexer_3 (
    .in0(multiplexer_1_out), .in1(3'b111), .out(multiplexer_3_out), .sel(Jal));
  RegisterFile registerfile_1 (
    .Register_D(multiplexer_3_out), .RegValue(multiplexer_2_out), .Register_S(rs), .Register_T(rt),
    .Write(RegWrt), .Clock(clk), .Reset(reset), .rsval(rsVal), .rtval(registerfile_1_rtval));
  assign bit_extender_2_out = {{10{Imm[5]}}, Imm};  // Bit_Extender bit_extender_2
  Multiplexer #(.width(16), .enable("false")) multiplexer_4 (
    .in0(registerfile_1_rtval), .in1(bit_extender_3_out), .out(multiplexer_4_out), .sel(ALUsrc));
  assign bit_extender_3_out = {{10{Imm[5]}}, Imm};  // Bit_Extender bit_extender_3
  Adder #(.width(16)) adder_2 (.a(adder_1_out), .b(bit_extender_2_out), .out(adder_2_out));  // open: cin, cout
  and and_1 (and_1_out, Branch, not_2_out);
  ALU alu_1 (.OpType(ALUop), .A(rsVal), .B(multiplexer_4_out), .Shamt(Shamt), .Result(alu_1_result), .Zero(alu_1_zero));
  not not_2 (not_2_out, alu_1_zero);
  Multiplexer #(.width(16), .enable("false")) multiplexer_5 (
    .in0(adder_1_out), .in1(adder_2_out), .out(multiplexer_5_out), .sel(and_1_out));
  assign bit_extender_4_out = {{4{1'b0}}, Add};  // Bit_Extender bit_extender_4
  not not_3 (not_3_out, clk);
  Multiplexer #(.width(16), .enable("false")) multiplexer_6 (
    .in0(multiplexer_5_out), .in1(bit_extender_4_out), .out(multiplexer_6_out), .sel(J));
  RAM #(.addrWidth(16), .dataWidth(16), .bus("separate")) ram_1 (
    .addr(alu_1_result), .din(registerfile_1_rtval), .data(ram_1_data), .str(MemWt), .clk(not_3_out),
    .ld(MemRd));  // open: sel, clr
  Multiplexer #(.width(16), .enable("false")) multiplexer_7 (
    .in0(multiplexer_6_out), .in1(rsVal), .out(multiplexer_7_out), .sel(Jr));
  Multiplexer #(.width(16), .enable("false")) multiplexer_8 (
    .in0(alu_1_result), .in1(ram_1_data), .out(multiplexer_8_out), .sel(MtR));
  Multiplexer #(.width(16), .enable("false")) multiplexer_9 (
    .in0(multiplexer_8_out), .in1(InputVal), .out(multiplexer_9_out), .sel(Input));

  // Other names for the same wires on the sheet: Rst = reset

  // Notes on the sheet:
  //   Instruction Memory
  //   contents of rom_1 (hex, n*v repeats v):
  //   2050 209f 3458 2070 2090 4458 c1ff 2fc1 c1ff
  //   Data Memory
endmodule

module ALU (
  input  [3:0] OpType,
  input  [15:0] A,
  input  [15:0] B,
  input  [2:0] Shamt,
  output [15:0] Result,
  output Zero
);

  wire comparator_1_lt;
  wire [3:0] bit_extender_1_out;
  wire [15:0] adder_1_out, and_1_out, bit_extender_2_out, not_1_out, or_1_out, shifter_1_out, shifter_2_out,
       subtractor_1_out, xor_1_out;

  assign bit_extender_1_out = {{1{1'b0}}, Shamt};  // Bit_Extender bit_extender_1
  assign not_1_out = ~A;  // NOT_Gate not_1, 16 bits wide
  assign xor_1_out = A ^ B;  // XOR_Gate xor_1, 16 bits wide
  assign and_1_out = A & B;  // AND_Gate and_1, 16 bits wide
  assign or_1_out = A | B;  // OR_Gate or_1, 16 bits wide
  Adder #(.width(16)) adder_1 (.a(A), .b(B), .out(adder_1_out));  // open: cin, cout
  Subtractor #(.width(16)) subtractor_1 (.a(A), .b(B), .out(subtractor_1_out));  // open: bin, bout
  Shifter #(.width(16), .shift("ar")) shifter_1 (.in(A), .\dist (bit_extender_1_out), .out(shifter_1_out));
  Shifter #(.width(16)) shifter_2 (.in(A), .\dist (bit_extender_1_out), .out(shifter_2_out));
  Comparator #(.width(16)) comparator_1 (.a(A), .b(B), .lt(comparator_1_lt));  // open: gt, eq
  assign bit_extender_2_out = {{15{1'b0}}, comparator_1_lt};  // Bit_Extender bit_extender_2
  Multiplexer #(.select(4), .width(16), .enable("false")) multiplexer_1 (
    .in0(not_1_out), .in1(xor_1_out), .in2(and_1_out), .in3(or_1_out), .in4(adder_1_out),
    .in5(subtractor_1_out), .in6(shifter_1_out), .in7(shifter_2_out), .in8(bit_extender_2_out), .out(Result),
    .sel(OpType));  // open: in9, in10, in11, in12, in13, in14, in15
  Comparator #(.width(16)) comparator_2 (.a(Result), .b({16{1'b0}}), .eq(Zero));  // open: gt, lt

  // Other names for the same wires on the sheet: OT[3:0] = OpType
endmodule

module PC (
  input  [15:0] Program,
  input  Clock,
  input  Reset,
  output [15:0] PC
);

  Register #(.width(16)) register_1 (.D(Program), .en(1'b1), .Q(PC), .clk(Clock), .clr(Reset));
endmodule

module Instruction_Decoder (
  input  [15:0] Instruction,
  output [2:0] shamt,
  output [2:0] rd,
  output [2:0] rt,
  output [2:0] rs,
  output [3:0] Opcode,
  output [5:0] Imm,
  output [11:0] Address
);


  assign Address = Instruction[11:0];
  assign Imm = Instruction[5:0];
  assign Opcode = Instruction[15:12];
  assign rd = Instruction[5:3];
  assign rs = Instruction[11:9];
  assign rt = Instruction[8:6];
  assign shamt = Instruction[2:0];
endmodule

module Controller (
  input  [3:0] Opcode,
  output Branch,
  output MemRead,
  output MemtoReg,
  output MemWrite,
  output ALUsrc,
  output RegDst,
  output Jump,
  output JR,
  output Jal,
  output Display,
  output Input,
  output [3:0] ALUop,
  output RegWrt
);

  wire decoder_1_out1, decoder_1_out2, decoder_1_out3, decoder_1_out4, decoder_1_out5, decoder_1_out6,
       decoder_1_out9, decoder_1_out12, or_1_out, or_7_out;

  Decoder #(.select(4), .enable("false")) decoder_1 (
    .out1(decoder_1_out1), .out2(decoder_1_out2), .out3(decoder_1_out3), .out4(decoder_1_out4),
    .out5(decoder_1_out5), .out6(decoder_1_out6), .out7(MemRead), .out8(MemWrite), .out9(decoder_1_out9),
    .out10(Jal), .out11(JR), .out12(decoder_1_out12), .out13(ALUop[3]), .out14(Input), .out15(Display),
    .sel(Opcode));  // open: out0
  or or_1 (or_1_out, MemWrite, decoder_1_out9, JR, decoder_1_out12, ALUop[3], Display);
  not not_1 (RegWrt, or_1_out);
  or or_2 (Branch, decoder_1_out12, ALUop[3]);
  or or_3 (ALUop[1], decoder_1_out5, decoder_1_out6);
  or or_4 (ALUop[2], decoder_1_out2, decoder_1_out3, decoder_1_out4, decoder_1_out5, decoder_1_out6, MemRead, MemWrite, decoder_1_out12);
  or or_5 (ALUop[0], decoder_1_out1, decoder_1_out4, decoder_1_out6, decoder_1_out12);
  or or_6 (ALUsrc, MemRead, decoder_1_out2, MemWrite);
  or or_7 (or_7_out, decoder_1_out2, MemRead);
  not not_2 (RegDst, or_7_out);
  or or_8 (Jump, decoder_1_out9, Jal);

  assign MemtoReg = MemRead;
endmodule

module RegisterFile (
  input  [2:0] Register_D,
  input  [15:0] RegValue,
  input  [2:0] Register_S,
  input  [2:0] Register_T,
  input  Write,
  input  Clock,
  input  Reset,
  output [15:0] rsval,
  output [15:0] rtval
);

  wire and_1_out, and_2_out, and_3_out, and_4_out, and_5_out, and_6_out, and_7_out, decoder_1_out1,
       decoder_1_out2, decoder_1_out3, decoder_1_out4, decoder_1_out5, decoder_1_out6, decoder_1_out7,
       decoder_2_out0, decoder_2_out1, decoder_2_out2, decoder_2_out3, decoder_2_out4, decoder_2_out5,
       decoder_2_out6, decoder_2_out7, decoder_3_out0, decoder_3_out1, decoder_3_out2, decoder_3_out3,
       decoder_3_out4, decoder_3_out5, decoder_3_out6, decoder_3_out7;
  wire [15:0] register_1_q, register_2_q, register_3_q, register_4_q, register_5_q, register_6_q,
       register_7_q, register_8_q;

  Register #(.width(16), .trigger("falling")) register_1 (
    .D({16{1'b0}}), .en(1'b0), .Q(register_1_q), .clk(Clock), .clr(Reset));
  // Probe on register_1_q
  and and_1 (and_1_out, Write, decoder_1_out1);
  Register #(.width(16), .trigger("falling")) register_2 (
    .D(RegValue), .en(and_1_out), .Q(register_2_q), .clk(Clock), .clr(Reset));
  // Probe on register_2_q
  and and_2 (and_2_out, Write, decoder_1_out2);
  Register #(.width(16), .trigger("falling")) register_3 (
    .D(RegValue), .en(and_2_out), .Q(register_3_q), .clk(Clock), .clr(Reset));
  // Probe on register_3_q
  Decoder #(.select(3), .enable("false")) decoder_1 (
    .out1(decoder_1_out1), .out2(decoder_1_out2), .out3(decoder_1_out3), .out4(decoder_1_out4),
    .out5(decoder_1_out5), .out6(decoder_1_out6), .out7(decoder_1_out7), .sel(Register_D));  // open: out0
  and and_3 (and_3_out, Write, decoder_1_out3);
  Register #(.width(16), .trigger("falling")) register_4 (
    .D(RegValue), .en(and_3_out), .Q(register_4_q), .clk(Clock), .clr(Reset));
  // Probe on register_4_q
  and and_4 (and_4_out, Write, decoder_1_out4);
  Register #(.width(16), .trigger("falling")) register_5 (
    .D(RegValue), .en(and_4_out), .Q(register_5_q), .clk(Clock), .clr(Reset));
  // Probe on register_5_q
  and and_5 (and_5_out, Write, decoder_1_out5);
  Register #(.width(16), .trigger("falling")) register_6 (
    .D(RegValue), .en(and_5_out), .Q(register_6_q), .clk(Clock), .clr(Reset));
  // Probe on register_6_q
  and and_6 (and_6_out, Write, decoder_1_out6);
  Register #(.width(16), .trigger("falling")) register_7 (
    .D(RegValue), .en(and_6_out), .Q(register_7_q), .clk(Clock), .clr(Reset));
  // Probe on register_7_q
  and and_7 (and_7_out, Write, decoder_1_out7);
  Register #(.width(16), .trigger("falling")) register_8 (
    .D(RegValue), .en(and_7_out), .Q(register_8_q), .clk(Clock), .clr(Reset));
  // Probe on register_8_q
  assign rtval = decoder_2_out1 ? register_2_q : 16'bz;  // Controlled_Buffer controlled_buffer_1
  assign rtval = decoder_2_out0 ? register_1_q : 16'bz;  // Controlled_Buffer controlled_buffer_2
  assign rtval = decoder_2_out5 ? register_6_q : 16'bz;  // Controlled_Buffer controlled_buffer_3
  assign rtval = decoder_2_out4 ? register_5_q : 16'bz;  // Controlled_Buffer controlled_buffer_4
  assign rtval = decoder_2_out3 ? register_4_q : 16'bz;  // Controlled_Buffer controlled_buffer_5
  assign rtval = decoder_2_out2 ? register_3_q : 16'bz;  // Controlled_Buffer controlled_buffer_6
  Decoder #(.select(3), .enable("false")) decoder_2 (
    .out0(decoder_2_out0), .out1(decoder_2_out1), .out2(decoder_2_out2), .out3(decoder_2_out3),
    .out4(decoder_2_out4), .out5(decoder_2_out5), .out6(decoder_2_out6), .out7(decoder_2_out7),
    .sel(Register_T));
  assign rtval = decoder_2_out7 ? register_8_q : 16'bz;  // Controlled_Buffer controlled_buffer_7
  assign rtval = decoder_2_out6 ? register_7_q : 16'bz;  // Controlled_Buffer controlled_buffer_8
  assign rsval = decoder_3_out3 ? register_4_q : 16'bz;  // Controlled_Buffer controlled_buffer_9
  assign rsval = decoder_3_out2 ? register_3_q : 16'bz;  // Controlled_Buffer controlled_buffer_10
  assign rsval = decoder_3_out1 ? register_2_q : 16'bz;  // Controlled_Buffer controlled_buffer_11
  assign rsval = decoder_3_out0 ? register_1_q : 16'bz;  // Controlled_Buffer controlled_buffer_12
  Decoder #(.select(3), .enable("false")) decoder_3 (
    .out0(decoder_3_out0), .out1(decoder_3_out1), .out2(decoder_3_out2), .out3(decoder_3_out3),
    .out4(decoder_3_out4), .out5(decoder_3_out5), .out6(decoder_3_out6), .out7(decoder_3_out7),
    .sel(Register_S));
  assign rsval = decoder_3_out7 ? register_8_q : 16'bz;  // Controlled_Buffer controlled_buffer_13
  assign rsval = decoder_3_out6 ? register_7_q : 16'bz;  // Controlled_Buffer controlled_buffer_14
  assign rsval = decoder_3_out5 ? register_6_q : 16'bz;  // Controlled_Buffer controlled_buffer_15
  assign rsval = decoder_3_out4 ? register_5_q : 16'bz;  // Controlled_Buffer controlled_buffer_16

  // Other names for the same wires on the sheet: clk = Clock; rd[2:0] = Register_D; rs[2:0] = Register_S; rst = Reset;
  //   rt[2:0] = Register_T; val[15:0] = RegValue; wrt = Write
endmodule
